// Logisim project flipflooop.circ as structural Verilog: 3 circuits, main circuit main
module main (
  input  in_1,
  input  in_2,
  input  in_3,
  input  in_4,
  input  in_5,
  input  in_6,
  input  in_7,
  input  in_8,
  input  in_9,
  input  in_10,
  input  in_11,
  input  in_12,
  input  in_13,
  input  in_14,
  input  in_15,
  input  in_16,
  input  in_17,
  input  in_18,
  input  in_19,
  input  in_20,
  input  in_21,
  input  in_22,
  input  in_23,
  input  in_24,
  input  in_25,
  input  in_26,
  input  in_27,
  input  in_28,
  input  in_29,
  input  in_30,
  input  in_31,
  input  in_32,
  input  in_33,
  input  in_34,
  input  in_35,
  input  in_36,
  output out_37,
  output out_38,
  output out_39,
  output out_40
);

  wire clock_1_out, CLOCK_2_out_2, CLOCK_2_out_3, CLOCK_2_out_4, CLOCK_2_out_5, CONTROLLER_out_9;

  Clock clock_1 (.out(clock_1_out));
  Controller CONTROLLER (
    .out_5(in_1), .out_7(in_5), .out_6(in_12), .out_8(in_24), .out_9(CONTROLLER_out_9), .in_1(CLOCK_2_out_2),
    .in_2(CLOCK_2_out_3), .in_3(CLOCK_2_out_4), .in_4(CLOCK_2_out_5));
  Counter CLOCK_2 (
    .in_1(clock_1_out), .out_2(CLOCK_2_out_2), .out_3(CLOCK_2_out_3), .out_4(CLOCK_2_out_4),
    .out_5(CLOCK_2_out_5));
  LED led_1 (.in(CONTROLLER_out_9));
  LED led_2 (.in(CONTROLLER_out_9));
  LED led_3 (.in(CONTROLLER_out_9));
  LED led_4 (.in(CONTROLLER_out_9));
  LED led_5 (.in(CONTROLLER_out_9));
  LED led_6 (.in(CONTROLLER_out_9));
  LED led_7 (.in(CONTROLLER_out_9));
  LED led_8 (.in(CONTROLLER_out_9));
  LED led_9 (.in(CONTROLLER_out_9));
  LED led_10 (.in(CONTROLLER_out_9));
  LED led_11 (.in(CONTROLLER_out_9));
  LED led_12 (.in(CONTROLLER_out_9));
  LED led_13 (.in(CONTROLLER_out_9));
  LED led_14 (.in(CONTROLLER_out_9));
  LED led_15 (.in(CONTROLLER_out_9));
  LED led_16 (.in(CONTROLLER_out_9));
  LED led_17 (.in(CONTROLLER_out_9));
  LED led_18 (.in(CONTROLLER_out_9));
  LED led_19 (.in(CONTROLLER_out_9));
  LED led_20 (.in(CONTROLLER_out_9));
  LED led_21 (.in(CONTROLLER_out_9));
  LED STATE_1 (.in(CONTROLLER_out_9));
  LED led_22 (.in(CONTROLLER_out_9));

  assign in_2 = in_1;
  assign in_3 = in_1;
  assign in_4 = in_1;
  assign in_6 = in_1;
  assign in_7 = in_5;
  assign in_8 = in_5;
  assign in_9 = in_1;
  assign in_10 = in_1;
  assign in_11 = in_5;
  assign in_13 = in_5;
  assign in_14 = in_1;
  assign in_15 = in_1;
  assign in_16 = in_12;
  assign in_17 = in_12;
  assign in_18 = in_5;
  assign in_19 = in_5;
  assign in_20 = in_12;
  assign in_21 = in_12;
  assign in_22 = in_5;
  assign in_23 = in_5;
  assign in_25 = in_12;
  assign in_26 = in_12;
  assign in_27 = in_24;
  assign in_28 = in_24;
  assign in_29 = in_12;
  assign in_30 = in_12;
  assign in_31 = in_24;
  assign in_32 = in_24;
  assign in_33 = in_24;
  assign in_34 = in_24;
  assign in_35 = in_24;
  assign in_36 = in_24;
endmodule

module Counter (
  input  in_1,
  output out_2,
  output out_3,
  output out_4,
  output out_5
);

  wire and_1_out, and_2_out, d_ff_1_qn, d_ff_2_qn, d_ff_3_qn, d_ff_4_qn;

  and and_1 (and_1_out, and_2_out, out_5);
  and and_2 (and_2_out, out_4, out_3);
  D_Flip_Flop d_ff_1 (.clk(in_1), .D(d_ff_1_qn), .Q(out_2), .Qn(d_ff_1_qn), .reset(and_1_out));  // open: preset, en
  D_Flip_Flop d_ff_2 (
    .clk(d_ff_1_qn), .D(d_ff_2_qn), .Q(out_3), .Qn(d_ff_2_qn), .reset(and_1_out));  // open: preset, en
  D_Flip_Flop d_ff_3 (
    .clk(d_ff_2_qn), .D(d_ff_3_qn), .Q(out_4), .Qn(d_ff_3_qn), .reset(and_1_out));  // open: preset, en
  D_Flip_Flop d_ff_4 (
    .clk(d_ff_3_qn), .D(d_ff_4_qn), .Q(out_5), .Qn(d_ff_4_qn), .reset(and_1_out));  // open: preset, en
endmodule

module Controller (
  input  in_1,
  input  in_2,
  input  in_3,
  input  in_4,
  output out_5,
  output out_6,
  output out_7,
  output out_8,
  output out_9
);

  wire _1_out, _3_out, _4_out, _5_out, _6_out, _7_out, _8_out, _9_out, _10_out, _11_out, _13_out, not_1_out,
       not_2_out, not_3_out, not_4_out;

  and _1 (_1_out, in_1, not_4_out, not_3_out, not_2_out);
  or STATE_5 (out_5, _13_out, _11_out, _10_out, _9_out);
  and _3 (_3_out, in_1, in_2, not_3_out, not_2_out);
  and _4 (_4_out, not_1_out, not_4_out, in_3, not_2_out);
  or STATE_4 (out_7, _13_out, _11_out, _8_out, _7_out);
  and _5 (_5_out, in_1, not_4_out, in_3, not_2_out);
  or STATE_3 (out_6, _11_out, _5_out, _6_out, _13_out);
  and _7 (_7_out, in_1, in_2, in_3, not_2_out);
  and _6 (_6_out, not_1_out, in_2, not_2_out, in_3);
  not not_1 (not_1_out, in_1);
  not not_2 (not_2_out, in_4);
  not not_3 (not_3_out, in_3);
  not not_4 (not_4_out, in_2);
  or STATE_2 (out_8, _13_out, _11_out, _4_out, _3_out);
  and _8 (_8_out, not_1_out, not_4_out, not_3_out, in_4);
  and _9 (_9_out, in_1, not_4_out, not_3_out, in_4);
  or STATE_1 (out_9, _1_out, _3_out, _4_out, _5_out, _6_out, _13_out, _7_out, _8_out, _9_out, _10_out, _11_out);
  and _10 (_10_out, not_1_out, in_2, not_3_out, in_4);
  and _13 (_13_out, in_1, not_4_out, in_3, in_4);
  and _11 (_11_out, in_1, in_2, not_3_out, in_4);
endmodule
